# Fritzing sketch RaspberryPi_GarageDoorOpener (saved by Fritzing 0.9.3b)
breadboards: 1

parts:
  Raspberry_Pi1 = Raspberry Pi 2
  R1 = Resistor [tolerance=±5% resistance=1k package=THT]
  Q1 = NPN-Transistor [package="TO92 [THT]"]
  D1 = Diode [package=diode-1n4001]
  S1 = SWITCH-MOMENTARY-2 [package=reed_switch_plastic]
  S2 = Reed switch [package=THT]  # not connected

nets:
  N1: Raspberry_Pi1.GPIO17, S1.1
  N2: Raspberry_Pi1.GPIO26, R1.Pin_0
  N3: Raspberry_Pi1.GND, Q1.E, S1.2
  N4: R1.Pin_1, Q1.B
  N5: Q1.C, D1.A

notes:
  Transistor is a BC337-025
  Resistor is 1K ohm
  Diode is 1N4007
  Relay is SRD-05VDC-SL-C 5V Relay
  Black = GND
  Red = 5V VCC
  Blue = IN (Signal)
  OUTPUT FOR RELAY TO GARAGE DOOR:
  Use "top 2", where the top is defined by the writing on the relay - this is "NC" operation. The top screw is the "NC" pin and the middle is the "C" pin.
  In this image, from Left to Right, the connectors are NC, C, NO (Normally Closed, Closed, Normally Open)
  This is a magnetic reed switch
